// Logisim project 8-bit-computer.circ as structural Verilog: 1 circuit, main circuit main
module main (
  input  IR_in,
  output out_2,
  output out_3,
  output out_4,
  output out_5,
  output out_6,
  output out_7,
  output out_8,
  output out_9
);

  wire and_1_out, and_2_out, Clock_out, not_1_out, or_1_out, or_3_out, or_4_out, or_6_out, or_7_out,
       or_9_out, or_10_out, or_12_out, or_13_out, or_15_out, or_16_out, or_18_out, or_19_out, or_21_out,
       or_22_out, or_24_out, or_25_out, or_26_out, or_27_out, or_28_out, or_29_out, or_30_out, or_31_out,
       or_32_out, or_33_out, or_34_out, or_35_out, or_36_out, or_37_out, or_38_out, or_39_out, or_40_out,
       or_41_out, or_42_out, or_43_out, or_44_out, or_45_out, or_46_out, or_47_out, or_48_out, or_49_out,
       or_50_out, or_51_out, or_52_out, or_53_out, or_54_out, or_55_out, or_56_out, xor_1_out, xor_2_out,
       xor_3_out;
  wire [7:0] rom_1_data, rom_2_data, rom_3_data, rom_4_data;
  wire [11:0] register_1_q;

  Clock Clock (.out(Clock_out));
  Register #(.width(1)) register_1 (.D(not_1_out), .en(1'b1), .Q(register_1_q[0]), .clk(Clock_out));  // open: clr
  Register #(.width(1)) register_2 (.D(xor_1_out), .en(1'b1), .Q(register_1_q[1]), .clk(Clock_out));  // open: clr
  Register #(.width(1)) register_3 (.D(xor_2_out), .en(1'b1), .Q(register_1_q[2]), .clk(Clock_out));  // open: clr
  Register #(.width(1)) register_4 (.D(xor_3_out), .en(1'b1), .Q(register_1_q[3]), .clk(Clock_out));  // open: clr
  Register #(.width(1)) register_5 (.D(out_9), .en(IR_in), .Q(register_1_q[4]), .clk(Clock_out));  // open: clr
  Register #(.width(1)) register_6 (.D(out_8), .en(IR_in), .Q(register_1_q[5]), .clk(Clock_out));  // open: clr
  Register #(.width(1)) register_7 (.D(out_7), .en(IR_in), .Q(register_1_q[6]), .clk(Clock_out));  // open: clr
  Register #(.width(1)) register_8 (.D(out_6), .en(IR_in), .Q(register_1_q[7]), .clk(Clock_out));  // open: clr
  Register #(.width(1)) register_9 (.D(out_5), .en(IR_in), .Q(register_1_q[8]), .clk(Clock_out));  // open: clr
  Register #(.width(1)) register_10 (.D(out_4), .en(IR_in), .Q(register_1_q[9]), .clk(Clock_out));  // open: clr
  Register #(.width(1)) register_11 (.D(out_3), .en(IR_in), .Q(register_1_q[10]), .clk(Clock_out));  // open: clr
  Register #(.width(1)) register_12 (.D(out_2), .en(IR_in), .Q(register_1_q[11]), .clk(Clock_out));  // open: clr
  not not_1 (not_1_out, register_1_q[0]);
  and and_1 (and_1_out, register_1_q[0], register_1_q[1]);
  and and_2 (and_2_out, and_1_out, register_1_q[2]);
  xor xor_1 (xor_1_out, register_1_q[0], register_1_q[1]);
  xor xor_2 (xor_2_out, and_1_out, register_1_q[2]);
  xor xor_3 (xor_3_out, and_2_out, register_1_q[3]);
  ROM #(.addrWidth(14)) rom_1 (.addr({2'b00, register_1_q}), .data(rom_1_data));  // open: sel
  ROM #(.addrWidth(14)) rom_2 (.addr({2'b01, register_1_q}), .data(rom_2_data));  // open: sel
  ROM #(.addrWidth(14)) rom_3 (.addr({2'b10, register_1_q}), .data(rom_3_data));  // open: sel
  ROM #(.addrWidth(14)) rom_4 (.addr({2'b11, register_1_q}), .data(rom_4_data));  // open: sel
  or or_1 (or_1_out, or_25_out, or_26_out);
  or or_2 (out_9, or_1_out, or_3_out);
  or or_3 (or_3_out, or_27_out, or_28_out);
  or or_4 (or_4_out, or_29_out, or_30_out);
  or or_5 (out_8, or_4_out, or_6_out);
  or or_6 (or_6_out, or_31_out, or_32_out);
  or or_7 (or_7_out, or_33_out, or_34_out);
  or or_8 (out_7, or_7_out, or_9_out);
  or or_9 (or_9_out, or_35_out, or_36_out);
  or or_10 (or_10_out, or_37_out, or_38_out);
  or or_11 (out_6, or_10_out, or_12_out);
  or or_12 (or_12_out, or_39_out, or_40_out);
  or or_13 (or_13_out, or_41_out, or_42_out);
  or or_14 (out_5, or_13_out, or_15_out);
  or or_15 (or_15_out, or_43_out, or_44_out);
  or or_16 (or_16_out, or_45_out, or_46_out);
  or or_17 (out_4, or_16_out, or_18_out);
  or or_18 (or_18_out, or_47_out, or_48_out);
  or or_19 (or_19_out, or_49_out, or_50_out);
  or or_20 (out_3, or_19_out, or_21_out);
  or or_21 (or_21_out, or_51_out, or_52_out);
  or or_22 (or_22_out, or_53_out, or_54_out);
  or or_23 (out_2, or_22_out, or_24_out);
  or or_24 (or_24_out, or_55_out, or_56_out);
  or or_25 (or_25_out, 1'b0, 1'b0);
  or or_26 (or_26_out, 1'b0, 1'b0);
  or or_27 (or_27_out, 1'b0, 1'b0);
  or or_28 (or_28_out, 1'b0, 1'b0);
  or or_29 (or_29_out, 1'b0, 1'b0);
  or or_30 (or_30_out, 1'b0, 1'b0);
  or or_31 (or_31_out, 1'b0, 1'b0);
  or or_32 (or_32_out, 1'b0, 1'b0);
  or or_33 (or_33_out, 1'b0, 1'b0);
  or or_34 (or_34_out, 1'b0, 1'b0);
  or or_35 (or_35_out, 1'b0, 1'b0);
  or or_36 (or_36_out, 1'b0, 1'b0);
  or or_37 (or_37_out, 1'b0, 1'b0);
  or or_38 (or_38_out, 1'b0, 1'b0);
  or or_39 (or_39_out, 1'b0, 1'b0);
  or or_40 (or_40_out, 1'b0, 1'b0);
  or or_41 (or_41_out, 1'b0, 1'b0);
  or or_42 (or_42_out, 1'b0, 1'b0);
  or or_43 (or_43_out, 1'b0, 1'b0);
  or or_44 (or_44_out, 1'b0, 1'b0);
  or or_45 (or_45_out, 1'b0, 1'b0);
  or or_46 (or_46_out, 1'b0, 1'b0);
  or or_47 (or_47_out, 1'b0, 1'b0);
  or or_48 (or_48_out, 1'b0, 1'b0);
  or or_49 (or_49_out, 1'b0, 1'b0);
  or or_50 (or_50_out, 1'b0, 1'b0);
  or or_51 (or_51_out, 1'b0, 1'b0);
  or or_52 (or_52_out, 1'b0, 1'b0);
  or or_53 (or_53_out, 1'b0, 1'b0);
  or or_54 (or_54_out, 1'b0, 1'b0);
  or or_55 (or_55_out, 1'b0, 1'b0);
  or or_56 (or_56_out, 1'b0, 1'b0);
endmodule
